# Fritzing sketch Sketch2 (saved by Fritzing 0.9.2b)
circuit board: 8.46667cm x 5.64444cm
breadboards: 1

parts:
  Part1 = Arduino Nano (Rev3.0)
  Power_plug1 = Power plug
  R1 = Resistor [tolerance=±5% resistance=330 package=THT]
  IR1 = TSOP312.., 314.. [package=THT]

nets:
  GND: Part1.GND, Power_plug1.GND, IR1.GND
  N1: Part1.D11/MOSI, IR1.Data
  VIN: Part1.VIN, Power_plug1.VCC
  N2: Part1.5V, R1.Pin_1
  N3: R1.Pin_0, IR1.Vs

notes:
  Adafruit 16 channel servo
  VCC
  SDA
  SCL
  GND
